# Fritzing sketch DHT-TINY-10A (saved by Fritzing 0.9.3b)
circuit board: 6.3cm x 5.3cm
breadboards: 1

parts:
  R1 = Resistor [tolerance=±5% resistance=100 package=THT]
  BLUE_LED = LED - 3mm [color="Blue (430nm)" package="3 mm [THT]"]
  R3 = Resistor [tolerance=±5% resistance=4.7k package=THT]
  ATtiny85 = attiny85 [package=dip]
  R2 = Resistor [tolerance=±5% resistance=10k package=THT]
  Reset = Pushbutton [package="[THT]"]
  DHT_SENSOR = DHT22 Humidity and Temperature Sensor
  HEADER = male pin header, 6 pins [form="♂ (male)"]
  ENABLE_LED = male pin header, 2 pins [form="♂ (male)"]

nets:
  N1: R1.Pin_0, ENABLE_LED.pin1
  N2: R1.Pin_1, BLUE_LED.anode
  GND: BLUE_LED.cathode, ATtiny85.Pin_4, Reset.Pin_1, Reset.Pin_2, HEADER.pin1
  5V: R3.Pin_0, ATtiny85.Pin_8, R2.Pin_0, DHT_SENSOR.VDD, HEADER.pin6
  N3: R3.Pin_1, ATtiny85.Pin_2, DHT_SENSOR.DATA
  N4: ATtiny85.Pin_1, R2.Pin_1, Reset.Pin_3, Reset.Pin_4, HEADER.pin2
  N5: ATtiny85.Pin_3, HEADER.pin3, ENABLE_LED.pin2
  N6: ATtiny85.Pin_5, HEADER.pin4
  N7: ATtiny85.Pin_6, DHT_SENSOR.GND
  N8: ATtiny85.Pin_7, HEADER.pin5

notes:
  by Daniel M. Porrey
  DHT Tiny
  Version 1.0a
  5V
  RST
  SDA
  SCL
  GND
  https://www.hackster.io/porrey
  https://github.com/porrey
  1
  3V3
  INT
  VDD
  DATA
  NULL
  SGND
  3
  4
  5
  6
  2
  GND/RST/INT/SDA/SCL/5V
  DHT-TINY-10A
