# Fritzing sketch DHT-TINY-10B (saved by Fritzing 0.9.3b)
circuit board: 2.1cm x 9cm
breadboards: 1

parts:
  R1 = Resistor [tolerance=±5% resistance=100 package=THT]
  R3 = Resistor [tolerance=±5% resistance=4.7k package=THT]
  ATtiny85 = attiny85 [package=dip]
  R2 = Resistor [tolerance=±5% resistance=10k package=THT]
  DHT_SENSOR = DHT22 Humidity and Temperature Sensor
  HEADER = male pin header, 6 pins [form="♂ (male)"]
  LED1 = LED - 3mm [color="Red (633nm)" package="3 mm [THT]"]

nets:
  N1: R1.Pin_0, ATtiny85.Pin_3, HEADER.pin3
  N2: R1.Pin_1, LED1.anode
  5V: R3.Pin_0, ATtiny85.Pin_8, R2.Pin_0, DHT_SENSOR.VDD, HEADER.pin6
  N3: R3.Pin_1, ATtiny85.Pin_2, DHT_SENSOR.DATA
  N4: ATtiny85.Pin_1, R2.Pin_1, HEADER.pin2
  GND: ATtiny85.Pin_4, HEADER.pin1, LED1.cathode
  N5: ATtiny85.Pin_5, HEADER.pin4
  N6: ATtiny85.Pin_6, DHT_SENSOR.GND
  N7: ATtiny85.Pin_7, HEADER.pin5

notes:
  by Daniel M. Porrey
  DHT Tiny
  Version 1.0b
  5V
  RST
  SDA
  SCL
  GND
  https://www.hackster.io/porrey
  https://github.com/porrey
  3V3
  INT
  1
  GND/RST/INT/SDA/SCL/5V
  DHT-TINY-10B
